# Fritzing sketch synchronous_camera_wiring (saved by Fritzing 0.9.10b)

parts:
  Mod1 = Raspberry Pi 4B
  R1 = Resistor [tolerance=±5% power=0.25 resistance=2.2k package=THT]
  R2 = Resistor [tolerance=±5% power=0.25 resistance=2.2k package=THT]

nets:
  N1: Mod1.3V3, R1.Pin_0
  N2: Mod1.GND, R2.Pin_1
  N3: R1.Pin_1, R2.Pin_0

notes:
  connect to camera XVS line
  connect to camera GND
